# Fritzing sketch led_strip_bling_bling (saved by Fritzing 0.9.2b)
circuit board: 1.36349cm x 2.32743cm
breadboards: 1

parts:
  U1 = attiny85 [package=dip]
  J1 = male pin header, 2 pins [form="♂ (male)"]
  J2 = male pin header, 3 pins [form="♂ (male)"]
  S1 = Pushbutton [package="[THT]"]

nets:
  N1: U1.Pin_2, S1.Pin_3, S1.Pin_4
  N2: U1.Pin_3, J2.pin3
  N3: U1.Pin_4, U1.Pin_5, J1.pin2, J2.pin1, S1.Pin_1, S1.Pin_2
  N4: U1.Pin_8, J1.pin1, J2.pin2

notes:
  +
  -
  +5V
  GND
  DATA IN
